# Fritzing sketch hall (saved by Fritzing 0.9.3b)
circuit board: 3.8cm x 1.2cm
breadboards: 1

parts:
  J1 = screw terminal, 2 pins
  U1 = ACS712 [package=so08]
  C2 = Ceramic Capacitor [capacitance=100nF package="200 mil [THT, multilayer]"]
  C1 = Ceramic Capacitor [capacitance=1nF package="100 mil [THT, multilayer]"]
  R1 = Resistor [tolerance=±5% resistance=220 package=THT]
  R2 = Resistor [tolerance=±5% resistance=220 package=THT]
  D1 = Schottky Diode [part_number=1N5817 package="300 mil [THT]"]
  J2 = female pin header, 3 pins [form="♀ (female)"]
  C3 = Ceramic Capacitor [capacitance=100nF package="100 mil [THT, multilayer]"]

nets:
  N1: J1.pin1, U1.IP+
  N2: J1.pin2, U1.IP-
  N3: U1.GND, C2.0, C1.0, R2.Pin_0, J2.pin3, C3.0
  N4: U1.FILT, C1.1
  N5: U1.VOUT, R1.Pin_0
  N6: U1.VCC, C2.1, J2.pin1
  N7: R1.Pin_1, R2.Pin_1, D1.anode
  N8: D1.cathode, J2.pin2, C3.1
