# Fritzing sketch smart-outlet (saved by Fritzing 0.9.3b)
circuit board: 8.46667cm x 5.64444cm
breadboards: 1

parts:
  D1 = Diode [part_number=1n4148 package=diode-1n4148]
  IC1 = LM741 [part_number=LM741 package=dip08]
  J1 = female pin header, 3 pins [form="♀ (female)" part_number="HALL Effect Sensor"]
  U2 = Voltage Regulator - 3.3V [package="TO220 [THT]"]
  R2 = Resistor [tolerance=±5% resistance=10k package=THT]
  U1 = ESP8266 WiFi Module [part_number=ESP8266]
  Q1 = NPN-Transistor [package="SOT-23 [SMD]"]
  R3 = Resistor [tolerance=±5% resistance=10k package=THT]
  U4 = RELAY [package=relay-jzc]
  D2 = Rectifier Diode [part_number=1N4001 package="300 mil [THT]"]
  L1 = Inductor [package="0805 [SMD]"]
  J2 = Screw terminal - 2 pins [part_number="220V IN" package=THT]
  J3 = Screw terminal - 2 pins [part_number="220V Out" package=THT]
  LED1 = LEDs [package=led10mm]
  R4 = Resistor [tolerance=±5% resistance=6.8k package=THT]
  S1 = SWITCH-MOMENTARY-2 [part_number=RESET package=tactile-pth-12mm]
  R5 = Resistor [tolerance=±5% resistance=100k package=THT]
  C1 = Electrolytic Capacitor [capacitance=1µF package="100 mil [THT, electrolytic]"]
  R6 = Resistor [tolerance=±5% resistance=2.2M package=THT]
  D3 = Diode [part_number=1n4148 package=diode-1n4148]
  R7 = Resistor [tolerance=±5% resistance=10k package=THT]
  R8 = Resistor [tolerance=±5% resistance=10k package=THT]
  R9 = Resistor [tolerance=±5% resistance=220k package=THT]
  C2 = Capacitor [part_number=220n package=cap-pth-small2]
  R10 = Resistor [tolerance=±5% resistance=1.5k package=THT]
  C3 = Capacitor [part_number=100n package=cap-pth-small2]
  C4 = Electrolytic Capacitor [capacitance=6.8µF package="100 mil [THT, electrolytic]"]
  R11 = Resistor [tolerance=±5% resistance=10k package=THT]
  C5 = Electrolytic Capacitor [capacitance=0.1µF package="100 mil [THT, electrolytic]"]
  C6 = Electrolytic Capacitor [capacitance=0.1µF package="100 mil [THT, electrolytic]"]
  S2 = SWITCH-MOMENTARY-2 [part_number=FLASH package=tactile-pth-12mm]
  R12 = Resistor [tolerance=±5% resistance=10k package=THT]
  C7 = Capacitor [part_number=100n package=cap-pth-small2]

nets:
  N1: D1.A, C1.-, D3.C
  N2: D1.C, R8.Pin_1, R9.Pin_0
  N3: IC1.+OFFSET, IC1.NC
  N4: IC1.-INPUT, R6.Pin_0, C2.2
  N5: IC1.+INPUT, R5.Pin_1
  -5V: IC1.V-
  N6: IC1.OUTPUT, C1.+, R6.Pin_1
  5V: IC1.V+, J1.pin1, U2.input_voltage, U4.COIL1, D2.cathode
  N7: J1.pin2, R5.Pin_0
  GND: J1.pin3, U2.GND, U1.GND, Q1.2, R4.Pin_0, S1.1, R10.Pin_0, C3.2, C4.-, C5.-, C6.-, S2.1, C7.2
  N8: U2.output_voltage, C7.1
  N9: R2.Pin_0, U1.CH_PD
  N10: R2.Pin_1, U1.VCC, R11.Pin_1, R12.Pin_1
  N11: U1.GPIO_0, R3.Pin_0
  N12: U1.GPIO_2, LED1.A
  N13: U1.ADC_0, R9.Pin_1, C3.1, C4.+
  N14: U1.REST, S1.2, R11.Pin_0, C5.+
  N15: Q1.0, R3.Pin_1
  N16: Q1.1, U4.COIL2, D2.anode
  N17: U4.NC, J3.pin1
  N18: U4.NO, L1.pin_0
  N19: L1.pin_1, J2.pin2
  N20: J2.pin1, J3.pin2
  N21: LED1.C, R4.Pin_1
  N22: R7.Pin_0, R8.Pin_0, C2.1, R10.Pin_1
  N23: C6.+, S2.2, R12.Pin_0

custom parts:
  LM741: General Purpose Operational Amplifier
